# Fritzing sketch bfg9000 (saved by Fritzing 0.8.3b)
circuit board: 10cm x 6cm
breadboards: 1

parts:
  Part1 = Arduino Fio (Funnel I/O)
  U2 = RELAY-SOLIDSTATE [package=relay-s108t02]
  U3 = RELAY-SOLIDSTATE [part_number=PCN-105D3MHZ,000 package=relay-s108t02]
  S1 = Pushbutton [package="[THT]"]
  Compressor_Pump = DC Motor
  Sprinker_Valve = Solenoid
  R1 = Resistor [tolerance=±5% resistance=1k package=THT]
  R2 = Resistor [tolerance=±5% resistance=1k package=THT]
  R3 = Resistor [tolerance=±5% resistance=1k package=THT]
  R4 = Resistor [tolerance=±5% resistance=1k package=THT]
  IC1 = IC, DIP package, 8 pins [chip_label=SSCDANN150PG2A3]
  S2 = SPST Switch [package=switch-spdt_kit]
  R5 = Resistor [tolerance=±5% resistance=220 package=THT]
  U4 = LIPO-2000mAh [package=lipo-2000]
  LCD1 = Adafruit Positive RGB 2x16 LCD  # not connected

nets:
  N1: Part1.VCC, Part1.D2, U2.T2, U3.T1, S1.Pin_3, S1.Pin_4, Compressor_Pump.pin_1, Sprinker_Valve.pin2, R3.Pin_1, R4.Pin_1, IC1.pin2, S2.P, R5.Pin_0, U4.+
  N2: Part1.GND, U2.T1, U2.-, U3.T2, U3.-, Compressor_Pump.pin_2, Sprinker_Valve.pin1, IC1.pin1, U4.-
  N3: Part1.D4, R2.Pin_0
  N4: Part1.D6_PWM, Part1.D7, R1.Pin_0
  N5: Part1.D8, S2.O
  N6: Part1.A4/SDA, R4.Pin_0, IC1.pin3
  N7: Part1.A5/SCL, R3.Pin_0, IC1.pin4
  N8: U2.+, R2.Pin_1
  N9: U3.+, R1.Pin_1
  N10: S1.Pin_1, S1.Pin_2
  N11: S2.S, R5.Pin_1

custom parts:
  Adafruit Positive RGB 2x16 LCD: Adafruit Positive 2x16 LCD Display with RGB Backlight
